# Fritzing sketch ThinkFreedomStack Schematic(Fritzing) (saved by Fritzing 0.9.2b)
breadboards: 3

parts:
  Part1 = Arduino Uno (Rev3)
  U1 = XBEE-1 [package=xbee-1_lock]
  SW1 = DIP SWITCH [package=dipswitch-02]
  SW2 = DIP SWITCH [package=dipswitch-02]
  X3 = USB Connectors [package=usb-a-s-silk-female]  # not connected
  SW3 = DIP SWITCH [package=dipswitch-02]
  SW4 = DIP SWITCH [package=dipswitch-02]
  S1 = Round Pushbutton
  R1 = Resistor [tolerance=±5% resistance=1k package=THT]
  U3 = XBEE-1 [package=xbee-1_lock]
  SW5 = DIP SWITCH [package=dipswitch-02]
  SW6 = DIP SWITCH [package=dipswitch-02]
  SW7 = DIP SWITCH [package=dipswitch-02]
  X4 = USB Connectors [package=usb-a-s-silk-female]
  SW8 = DIP SWITCH [package=dipswitch-02]
  Raspberry_Pi1 = Raspberry Pi 2
  SW9 = DIP SWITCH [package=dipswitch-02]
  Raspberry_Pi2 = Raspberry Pi B rev2  # not connected
  LED1 = smd LED [color="Red (633nm)" package="1206 [SMD]"]
  R2 = Resistor [tolerance=±5% resistance=220 package="0402 [SMD]"]
  Part2 = Arduino Micro (Rev3)

nets:
  N1: Part1.GND, Part1.D5_PWM, SW3.1, R1.Pin_1, SW9.3
  N2: Part1.D0/RX, SW1.3, SW2.4
  N3: Part1.D1/TX, SW1.4, SW2.3
  N4: Part1.3V3, SW9.4
  N5: Part1.5V, S1.leg0
  N6: U1.DOUT, SW1.2, SW2.2, SW4.1
  N7: U1.DIN, SW1.1, SW2.1, SW3.2
  N8: U1.GND, SW9.2
  N9: S1.leg1, R1.Pin_0
  N10: U3.VDD, SW5.1
  N11: U3.DOUT, SW6.1, SW8.1
  N12: U3.DIN, SW6.2, SW7.2
  N13: U3.RSSI, R2.Pin_1
  N14: U3.GND, SW5.2
  GND: SW5.3, SW7.1, Raspberry_Pi1.GND, LED1.cathode, Part2.GND
  N15: SW5.4, Raspberry_Pi1.3v3
  N16: SW6.3, Raspberry_Pi1.GPIO14
  N17: SW6.4, Raspberry_Pi1.GPIO15
  N18: SW7.3, X4.D-
  N19: SW7.4, X4.GND
  N20: X4.D+, SW8.4
  N21: Raspberry_Pi1.GPIO21, Part2.D4_PWM/A6
  N22: LED1.anode, R2.Pin_0
